// Logisim project Full_adder.circ as structural Verilog: 2 circuits, main circuit main
module main (
  input  c_in,
  output out_2
);

  wire A_sw1, A_sw2, A_sw3, A_sw4, B_p1, B_p2, B_p3, B_p4, fulladder_1_c_out, fulladder_1_s,
       fulladder_2_c_out, fulladder_2_s, fulladder_3_c_out, fulladder_3_s, fulladder_4_s;

  FullAdder fulladder_1 (.B(B_p1), .A(A_sw1), .c_in(c_in), .c_out(fulladder_1_c_out), .S(fulladder_1_s));
  // DipSwitch #(.number(4)) B: pin names not known; wires that end beside it: B_p1, B_p2, B_p3, B_p4
  FullAdder fulladder_2 (.B(B_p2), .A(A_sw2), .c_in(fulladder_1_c_out), .c_out(fulladder_2_c_out), .S(fulladder_2_s));
  DipSwitch #(.number(4)) A (.sw1(A_sw1), .sw2(A_sw2), .sw3(A_sw3), .sw4(A_sw4));
  _7_Segment_Display u_7_segment_display_1 (
    .e(fulladder_4_s), .d(fulladder_3_s), .c(fulladder_2_s), .dp(fulladder_1_s));  // open: g, f, a, b
  FullAdder fulladder_3 (.B(B_p3), .A(A_sw3), .c_in(fulladder_2_c_out), .c_out(fulladder_3_c_out), .S(fulladder_3_s));
  FullAdder fulladder_4 (.B(B_p4), .A(A_sw4), .c_in(fulladder_3_c_out), .c_out(out_2), .S(fulladder_4_s));
endmodule

module FullAdder (
  input  B,
  input  A,
  input  c_in,
  output c_out,
  output S
);

  wire and_1_out, and_2_out, xor_1_out;

  or or_1 (c_out, and_1_out, and_2_out);
  and and_1 (and_1_out, A, B);
  and and_2 (and_2_out, xor_1_out, c_in);
  xor xor_1 (xor_1_out, B, A);
  xor xor_2 (S, xor_1_out, c_in);
endmodule
