// Logisim project Decod.circ as structural Verilog: 2 circuits, main circuit main
module main (
  input  in_1,
  input  in_2,
  input  in_3,
  output Y0,
  output Y1,
  output Y2,
  output Y3,
  output Y4,
  output Y5,
  output Y6,
  output Y7
);

  wire not_1_out;

  // Probe on in_1
  not not_1 (not_1_out, in_1);
  // Probe on not_1_out
  Decoder_subcircuit decoder_subcircuit_1 (.En(not_1_out), .A(in_3), .B(in_2), .y0(Y0), .y1(Y1), .y2(Y2), .y3(Y3));
  Decoder_subcircuit decoder_subcircuit_2 (.En(in_1), .A(in_3), .B(in_2), .y0(Y4), .y1(Y5), .y2(Y6), .y3(Y7));
endmodule

module Decoder_subcircuit (
  input  En,
  input  A,
  input  B,
  output y0,
  output y1,
  output y2,
  output y3
);

  wire not_1_out, not_2_out;

  not not_1 (not_1_out, A);
  not not_2 (not_2_out, B);
  and and_1 (y0, not_1_out, En, not_2_out);
  and and_2 (y1, A, En, not_2_out);
  and and_3 (y2, not_1_out, En, B);
  and and_4 (y3, A, En, B);
endmodule
