// Logisim project Encoder.circ as structural Verilog: 1 circuit, main circuit main
module main (
);

  // DipSwitch dipswitch_1: pin names not known
  // OR_Gate or_1 is placed but not wired
  // OR_Gate or_2 is placed but not wired
  // OR_Gate or_3 is placed but not wired
  // OR_Gate or_4 is placed but not wired
  _7_Segment_Display u_7_segment_display_1 ();  // open: g, f, a, b, e, d, c, dp
endmodule
