// Logisim project PriorityEncoder.circ as structural Verilog: 2 circuits, main circuit main
module main (
);

  wire dipswitch_1_p1, dipswitch_1_p3, dipswitch_1_p4, dipswitch_1_p5, dipswitch_1_p6, dipswitch_1_p7,
       dipswitch_1_p8, dipswitch_1_p9, dipswitch_1_p10, dipswitch_1_p11, dipswitch_1_p12, dipswitch_1_p13,
       dipswitch_1_p14, dipswitch_1_p15, dipswitch_1_p16, dipswitch_1_p17, pe_1_v, pe_1_y0, pe_1_y1, pe_2_v,
       pe_2_y0, pe_2_y1, pe_3_v, pe_3_y0, pe_3_y1, pe_4_v, pe_4_y0, pe_4_y1, pe_5_v;
  wire [1:0] multiplexer_2_out, pe_5_y1;

  // DipSwitch #(.number(16)) dipswitch_1: pin names not known; wires that end beside it: dipswitch_1_p1, dipswitch_1_p1, dipswitch_1_p3, dipswitch_1_p4, dipswitch_1_p5, dipswitch_1_p6, dipswitch_1_p7, dipswitch_1_p8, dipswitch_1_p9, dipswitch_1_p10, dipswitch_1_p11, dipswitch_1_p12, dipswitch_1_p13, dipswitch_1_p14, dipswitch_1_p15, dipswitch_1_p16, dipswitch_1_p17, dipswitch_1_p3, dipswitch_1_p4, dipswitch_1_p15, dipswitch_1_p5, dipswitch_1_p14
  PE pe_1 (.V(pe_1_v), .Y1(pe_1_y1), .Y0(pe_1_y0));  // open: A3, A2, A1, A0
  PE pe_2 (
    .A3(dipswitch_1_p9), .A2(dipswitch_1_p8), .A1(dipswitch_1_p7), .A0(dipswitch_1_p6), .V(pe_2_v),
    .Y1(pe_2_y1), .Y0(pe_2_y0));
  PE pe_3 (
    .A3(dipswitch_1_p13), .A2(dipswitch_1_p12), .A1(dipswitch_1_p11), .A0(dipswitch_1_p10), .V(pe_3_v),
    .Y1(pe_3_y1), .Y0(pe_3_y0));
  PE pe_4 (.V(pe_4_v), .Y1(pe_4_y1), .Y0(pe_4_y0));  // open: A3, A2, A1, A0
  Multiplexer #(.select(2)) multiplexer_1 (
    .in0(pe_1_y1), .in1(pe_2_y1), .in2(pe_3_y1), .in3(pe_4_y1), .out(multiplexer_2_out[1]), .sel(pe_5_y1));
  Multiplexer #(.select(2)) multiplexer_2 (
    .in0(pe_1_y0), .in1(pe_2_y0), .in2(pe_3_y0), .in3(pe_4_y0), .out(multiplexer_2_out[0]), .sel(pe_5_y1));
  PE pe_5 (.A3(pe_1_v), .A2(pe_2_v), .A1(pe_3_v), .A0(pe_4_v), .V(pe_5_v), .Y1(pe_5_y1[0]), .Y0(pe_5_y1[1]));
  Hex_Digit_Display hex_digit_display_1 (.value({pe_5_y1, multiplexer_2_out}));  // open: dp
endmodule

module PE (
  input  A3,
  input  A2,
  input  A1,
  input  A0,
  output V,
  output Y1,
  output Y0
);

  wire and_1_out;

  and and_1 (and_1_out, ~A2, A1);  // AND_Gate
  or or_1 (V, A3, A2, A1, A0);
  or or_2 (Y1, A2, A3);
  or or_3 (Y0, A3, and_1_out);
endmodule
