// Logisim project selector_2to1.circ as structural Verilog: 1 circuit, main circuit main
module main (
  input  D0,
  input  S,
  input  D1,
  output out_4
);

  wire and_1_out, and_2_out, decoder_1_out0, decoder_1_out1;

  Decoder #(.enable("false")) decoder_1 (.out0(decoder_1_out0), .out1(decoder_1_out1), .sel(S));
  and and_1 (and_1_out, D0, decoder_1_out0);
  and and_2 (and_2_out, decoder_1_out1, D1);
  or or_1 (out_4, and_1_out, and_2_out);
endmodule
