// Logisim project selector_4to1.circ as structural Verilog: 1 circuit, main circuit main
module main (
  input  [2:0] in_1,
  input  [2:0] in_2,
  input  [2:0] in_3,
  input  in_4
);

  // AND_Gate and_1 is placed but not wired
  // AND_Gate and_2 is placed but not wired
  // OR_Gate or_1 is placed but not wired
endmodule
