// Logisim project O.circ as structural Verilog: 1 circuit, main circuit main
module main (
  input  Cin,
  input  A,
  input  B
);

  wire adder_1_cout, xor_1_out;

  Adder #(.width(1)) adder_1 (.a(A), .b(B), .cin(Cin), .cout(adder_1_cout));  // open: out
  xor xor_1 (xor_1_out, Cin, adder_1_cout);
  LED Overflow (.in(xor_1_out));
endmodule
