// Logisim project sign_magnitude_adder.circ as structural Verilog: 1 circuit, main circuit main
module main (
  input  [3:0] in_1,
  input  [3:0] in_2
);

  wire multiplexer_1_out, multiplexer_3_out, subtractor_1_bout, xor_1_out;
  wire [2:0] adder_1_out, multiplexer_2_out, multiplexer_4_out, subtractor_1_out, subtractor_2_out;

  _7_Segment_Display u_7_segment_display_1 (.g(in_1[3]));  // open: f, a, b, e, d, c, dp
  Hex_Digit_Display hex_digit_display_1 (.value({1'b0, in_1[2:0]}));  // open: dp
  _7_Segment_Display u_7_segment_display_2 (.g(in_2[3]));  // open: f, a, b, e, d, c, dp
  Hex_Digit_Display hex_digit_display_2 (.value({1'b0, in_2[2:0]}));  // open: dp
  xor xor_1 (xor_1_out, in_1[3], in_2[3]);
  Multiplexer multiplexer_1 (.in0(in_1[3]), .in1(in_2[3]), .out(multiplexer_1_out), .sel(subtractor_1_bout));
  Adder #(.width(3)) adder_1 (.a(in_1[2:0]), .b(in_2[2:0]), .out(adder_1_out));  // open: cin, cout
  Subtractor #(.width(3)) subtractor_1 (
    .a(in_1[2:0]), .b(in_2[2:0]), .out(subtractor_1_out), .bout(subtractor_1_bout));  // open: bin
  Subtractor #(.width(3)) subtractor_2 (.a(in_2[2:0]), .b(in_1[2:0]), .out(subtractor_2_out));  // open: bin, bout
  Multiplexer #(.width(3)) multiplexer_2 (
    .in0(subtractor_1_out), .in1(subtractor_2_out), .out(multiplexer_2_out), .sel(subtractor_1_bout));
  Multiplexer multiplexer_3 (.in0(in_1[3]), .in1(multiplexer_1_out), .out(multiplexer_3_out), .sel(xor_1_out));
  Multiplexer #(.width(3)) multiplexer_4 (
    .in0(adder_1_out), .in1(multiplexer_2_out), .out(multiplexer_4_out), .sel(xor_1_out));
  _7_Segment_Display u_7_segment_display_3 (.g(multiplexer_3_out));  // open: f, a, b, e, d, c, dp
  Hex_Digit_Display hex_digit_display_3 (.value({1'b0, multiplexer_4_out}));  // open: dp
endmodule
