// Logisim project sub.circ as structural Verilog: 2 circuits, main circuit main
module main (
  input  c_in
);

  wire fulladder_1_c_out, fulladder_2_c_out, fulladder_3_c_out, fulladder_4_c_out, not_1_out, not_2_out,
       not_3_out, not_4_out, not_5_out;
  wire [3:0] A_sw1, B_p1, fulladder_1_s;

  FullAdder fulladder_1 (.B(not_2_out), .A(A_sw1[0]), .c_in(c_in), .c_out(fulladder_1_c_out), .S(fulladder_1_s[0]));
  not not_1 (not_1_out, B_p1[1]);
  not not_2 (not_2_out, B_p1[0]);
  // DipSwitch #(.number(4)) B: pin names not known; wires that end beside it: B_p1[0], B_p1[1], B_p1[2], B_p1[3]
  not not_3 (not_3_out, B_p1[2]);
  not not_4 (not_4_out, B_p1[3]);
  FullAdder fulladder_2 (
    .B(not_1_out), .A(A_sw1[1]), .c_in(fulladder_1_c_out), .c_out(fulladder_2_c_out), .S(fulladder_1_s[1]));
  DipSwitch #(.number(4)) A (.sw1(A_sw1[0]), .sw2(A_sw1[1]), .sw3(A_sw1[2]), .sw4(A_sw1[3]));
  Hex_Digit_Display hex_digit_display_1 (.value(fulladder_1_s));  // open: dp
  Hex_Digit_Display hex_digit_display_2 (.value(B_p1));  // open: dp
  Hex_Digit_Display hex_digit_display_3 (.value(A_sw1));  // open: dp
  FullAdder fulladder_3 (
    .B(not_3_out), .A(A_sw1[2]), .c_in(fulladder_2_c_out), .c_out(fulladder_3_c_out), .S(fulladder_1_s[2]));
  FullAdder fulladder_4 (
    .B(not_4_out), .A(A_sw1[3]), .c_in(fulladder_3_c_out), .c_out(fulladder_4_c_out), .S(fulladder_1_s[3]));
  not not_5 (not_5_out, fulladder_4_c_out);
  LED Borrow (.in(not_5_out));
endmodule

module FullAdder (
  input  B,
  input  A,
  input  c_in,
  output c_out,
  output S
);

  wire and_1_out, and_2_out, xor_1_out;

  or or_1 (c_out, and_1_out, and_2_out);
  and and_1 (and_1_out, A, B);
  and and_2 (and_2_out, xor_1_out, c_in);
  xor xor_1 (xor_1_out, B, A);
  xor xor_2 (S, xor_1_out, c_in);
endmodule
