// Logisim project sr.circ as structural Verilog: 1 circuit, main circuit main
module main (
  output Q,
  output Q_bar
);

  wire and_1_out, and_2_out, dipswitch_1_p1, dipswitch_2_p1, dipswitch_3_p1;

  // DipSwitch #(.number(1)) dipswitch_1: pin names not known; wires that end beside it: dipswitch_1_p1
  // DipSwitch #(.number(1)) dipswitch_2: pin names not known; wires that end beside it: dipswitch_2_p1
  // DipSwitch #(.number(1)) dipswitch_3: pin names not known; wires that end beside it: dipswitch_3_p1
  and and_1 (and_1_out, dipswitch_1_p1, dipswitch_2_p1);
  and and_2 (and_2_out, dipswitch_3_p1, dipswitch_2_p1);
  nor nor_1 (Q, and_1_out, Q_bar);
  nor nor_2 (Q_bar, Q, and_2_out);
endmodule
